# Fritzing sketch SmallQlockArduino (saved by Fritzing 0.7.0b)
breadboards: 1

parts:
  Arduino = Arduino Nano v2.3
  Plug = Power plug
  RTC = female pin header, 2 pins [form="♂ (male)"]
  LC1 = female pin header, 3 pins [form="♀ (female)"]
  LC2 = female pin header, 3 pins [form="♀ (female)"]
  J2 = female pin header, 8 pins [form="♀ (female)"]
  J4 = female pin header, 2 pins [form="♀ (female)"]
  J3 = female pin header, 2 pins [form="♀ (female)"]

nets:
  GND: Arduino.GND, Plug.GND, J2.pin1, J2.pin2, J2.pin3, J2.pin4
  N1: Arduino.D2, LC1.pin1
  N2: Arduino.D3, LC1.pin2
  N3: Arduino.D4, LC1.pin3
  N4: Arduino.D5, LC2.pin1
  N5: Arduino.D6, LC2.pin2
  N6: Arduino.D7, LC2.pin3
  N7: Arduino.D9, J4.pin1
  N8: Arduino.D10, J4.pin2
  N9: Arduino.D11, J3.pin2
  N10: Arduino.D12, J3.pin1
  N11: Arduino.A5, RTC.pin1
  N12: Arduino.A4, RTC.pin2
  N13: Arduino.+5V, J2.pin5, J2.pin6, J2.pin7, J2.pin8
  VIN: Arduino.VIN, Plug.VCC

notes:
  |-5v-|
  |-gnd-|
  sda
  scl
  min
  bright
  hour
  mode
  data
  load
  clk
