# Fritzing sketch SmallQlockButtons (saved by Fritzing 0.7.0b)
breadboards: 1

parts:
  S1 = Pushbutton [package="[THT]"]
  S2 = Pushbutton [package="[THT]"]
  S3 = Pushbutton [package="[THT]"]
  J1 = female pin header, 2 pins [form="♀ (female)"]
  R1 = Resistor [tolerance=±5% resistance=220 package=THT]
  R2 = Resistor [tolerance=±5% resistance=220 package=THT]
  R3 = Resistor [tolerance=±5% resistance=220 package=THT]
  R4 = Resistor [tolerance=±5% resistance=220 package=THT]
  J2 = female pin header, 4 pins [form="♀ (female)"]
  S4 = Pushbutton [package="[THT]"]

nets:
  N1: S1.Pin_1, S1.Pin_2, R1.Pin_0, J2.pin1
  N2: S1.Pin_3, S1.Pin_4, S2.Pin_3, S2.Pin_4, S3.Pin_3, S3.Pin_4, J1.pin1, S4.Pin_3, S4.Pin_4
  N3: S2.Pin_1, S2.Pin_2, R2.Pin_0, J2.pin2
  N4: S3.Pin_1, S3.Pin_2, R3.Pin_0, J2.pin3
  N5: J1.pin2, R1.Pin_1, R2.Pin_1, R3.Pin_1, R4.Pin_1
  N6: R4.Pin_0, J2.pin4, S4.Pin_1, S4.Pin_2

notes:
  v
  gnd
  1
  4
  3
  2
