# Fritzing sketch SmallQlockLED (saved by Fritzing 0.7.0b)
breadboards: 4

parts:
  MAX1 = MAX7219
  R1 = Resistor [tolerance=±5% resistance=22k package=THT]
  C1 = Ceramic Capacitor [capacitance=0.1µF package="100 mil [THT, multilayer]"]
  MAX2 = MAX7219
  R2 = Resistor [tolerance=±5% resistance=22k package=THT]
  C3 = Ceramic Capacitor [capacitance=0.1µF package="100 mil [THT, multilayer]"]
  C4 = Electrolytic Capacitor [capacitance=1µF package="100 mil [THT, electrolytic]"]
  J2 = female pin header, 3 pins [form="♀ (female)"]
  LED115 = White 1210 smd LED [package="1210 [SMD]"]
  LED116 = White 1210 smd LED [package="1210 [SMD]"]
  LED117 = White 1210 smd LED [package="1210 [SMD]"]
  LED118 = White 1210 smd LED [package="1210 [SMD]"]
  LED119 = White 1210 smd LED [package="1210 [SMD]"]
  LED120 = White 1210 smd LED [package="1210 [SMD]"]
  LED121 = White 1210 smd LED [package="1210 [SMD]"]
  LED122 = White 1210 smd LED [package="1210 [SMD]"]
  LED123 = White 1210 smd LED [package="1210 [SMD]"]
  LED124 = White 1210 smd LED [package="1210 [SMD]"]
  LED125 = White 1210 smd LED [package="1210 [SMD]"]
  LED126 = White 1210 smd LED [package="1210 [SMD]"]
  LED127 = White 1210 smd LED [package="1210 [SMD]"]
  LED128 = White 1210 smd LED [package="1210 [SMD]"]
  LED129 = White 1210 smd LED [package="1210 [SMD]"]
  LED130 = White 1210 smd LED [package="1210 [SMD]"]
  LED131 = White 1210 smd LED [package="1210 [SMD]"]
  LED132 = White 1210 smd LED [package="1210 [SMD]"]
  LED133 = White 1210 smd LED [package="1210 [SMD]"]
  LED134 = White 1210 smd LED [package="1210 [SMD]"]
  LED135 = White 1210 smd LED [package="1210 [SMD]"]
  LED136 = White 1210 smd LED [package="1210 [SMD]"]
  LED137 = White 1210 smd LED [package="1210 [SMD]"]
  LED138 = White 1210 smd LED [package="1210 [SMD]"]
  LED139 = White 1210 smd LED [package="1210 [SMD]"]
  LED140 = White 1210 smd LED [package="1210 [SMD]"]
  LED141 = White 1210 smd LED [package="1210 [SMD]"]
  LED142 = White 1210 smd LED [package="1210 [SMD]"]
  LED143 = White 1210 smd LED [package="1210 [SMD]"]
  LED144 = White 1210 smd LED [package="1210 [SMD]"]
  LED145 = White 1210 smd LED [package="1210 [SMD]"]
  LED146 = White 1210 smd LED [package="1210 [SMD]"]
  LED147 = White 1210 smd LED [package="1210 [SMD]"]
  LED148 = White 1210 smd LED [package="1210 [SMD]"]
  LED149 = White 1210 smd LED [package="1210 [SMD]"]
  LED150 = White 1210 smd LED [package="1210 [SMD]"]
  LED151 = White 1210 smd LED [package="1210 [SMD]"]
  LED152 = White 1210 smd LED [package="1210 [SMD]"]
  LED153 = White 1210 smd LED [package="1210 [SMD]"]
  LED154 = White 1210 smd LED [package="1210 [SMD]"]
  LED155 = White 1210 smd LED [package="1210 [SMD]"]
  LED156 = White 1210 smd LED [package="1210 [SMD]"]
  LED157 = White 1210 smd LED [package="1210 [SMD]"]
  LED158 = White 1210 smd LED [package="1210 [SMD]"]
  LED159 = White 1210 smd LED [package="1210 [SMD]"]
  LED160 = White 1210 smd LED [package="1210 [SMD]"]
  LED161 = White 1210 smd LED [package="1210 [SMD]"]
  LED162 = White 1210 smd LED [package="1210 [SMD]"]
  LED163 = White 1210 smd LED [package="1210 [SMD]"]
  LED164 = White 1210 smd LED [package="1210 [SMD]"]
  LED165 = White 1210 smd LED [package="1210 [SMD]"]
  LED166 = White 1210 smd LED [package="1210 [SMD]"]
  LED167 = White 1210 smd LED [package="1210 [SMD]"]
  LED168 = White 1210 smd LED [package="1210 [SMD]"]
  LED169 = White 1210 smd LED [package="1210 [SMD]"]
  LED170 = White 1210 smd LED [package="1210 [SMD]"]
  LED171 = White 1210 smd LED [package="1210 [SMD]"]
  LED172 = White 1210 smd LED [package="1210 [SMD]"]
  LED173 = White 1210 smd LED [package="1210 [SMD]"]
  LED174 = White 1210 smd LED [package="1210 [SMD]"]
  LED175 = White 1210 smd LED [package="1210 [SMD]"]
  LED176 = White 1210 smd LED [package="1210 [SMD]"]
  LED177 = White 1210 smd LED [package="1210 [SMD]"]
  LED178 = White 1210 smd LED [package="1210 [SMD]"]
  LED179 = White 1210 smd LED [package="1210 [SMD]"]
  LED180 = White 1210 smd LED [package="1210 [SMD]"]
  LED181 = White 1210 smd LED [package="1210 [SMD]"]
  LED182 = White 1210 smd LED [package="1210 [SMD]"]
  LED183 = White 1210 smd LED [package="1210 [SMD]"]
  LED184 = White 1210 smd LED [package="1210 [SMD]"]
  LED185 = White 1210 smd LED [package="1210 [SMD]"]
  LED186 = White 1210 smd LED [package="1210 [SMD]"]
  LED187 = White 1210 smd LED [package="1210 [SMD]"]
  LED188 = White 1210 smd LED [package="1210 [SMD]"]
  LED189 = White 1210 smd LED [package="1210 [SMD]"]
  LED190 = White 1210 smd LED [package="1210 [SMD]"]
  LED191 = White 1210 smd LED [package="1210 [SMD]"]
  LED192 = White 1210 smd LED [package="1210 [SMD]"]
  LED193 = White 1210 smd LED [package="1210 [SMD]"]
  LED194 = White 1210 smd LED [package="1210 [SMD]"]
  LED195 = White 1210 smd LED [package="1210 [SMD]"]
  LED196 = White 1210 smd LED [package="1210 [SMD]"]
  LED197 = White 1210 smd LED [package="1210 [SMD]"]
  LED198 = White 1210 smd LED [package="1210 [SMD]"]
  LED199 = White 1210 smd LED [package="1210 [SMD]"]
  LED200 = White 1210 smd LED [package="1210 [SMD]"]
  LED201 = White 1210 smd LED [package="1210 [SMD]"]
  LED202 = White 1210 smd LED [package="1210 [SMD]"]
  LED203 = White 1210 smd LED [package="1210 [SMD]"]
  LED204 = White 1210 smd LED [package="1210 [SMD]"]
  LED205 = White 1210 smd LED [package="1210 [SMD]"]
  LED206 = White 1210 smd LED [package="1210 [SMD]"]
  LED207 = White 1210 smd LED [package="1210 [SMD]"]
  LED208 = White 1210 smd LED [package="1210 [SMD]"]
  LED209 = White 1210 smd LED [package="1210 [SMD]"]
  LED210 = White 1210 smd LED [package="1210 [SMD]"]
  LED211 = White 1210 smd LED [package="1210 [SMD]"]
  LED212 = White 1210 smd LED [package="1210 [SMD]"]
  LED213 = White 1210 smd LED [package="1210 [SMD]"]
  LED214 = White 1210 smd LED [package="1210 [SMD]"]
  LED215 = White 1210 smd LED [package="1210 [SMD]"]
  LED216 = White 1210 smd LED [package="1210 [SMD]"]
  LED217 = White 1210 smd LED [package="1210 [SMD]"]
  LED218 = White 1210 smd LED [package="1210 [SMD]"]
  LED219 = White 1210 smd LED [package="1210 [SMD]"]
  LED220 = White 1210 smd LED [package="1210 [SMD]"]
  LED221 = White 1210 smd LED [package="1210 [SMD]"]
  LED222 = White 1210 smd LED [package="1210 [SMD]"]
  LED223 = White 1210 smd LED [package="1210 [SMD]"]
  LED224 = White 1210 smd LED [package="1210 [SMD]"]
  LED225 = White 1210 smd LED [package="1210 [SMD]"]
  LED226 = White 1210 smd LED [package="1210 [SMD]"]
  LED227 = White 1210 smd LED [package="1210 [SMD]"]
  LED228 = White 1210 smd LED [package="1210 [SMD]"]
  J3 = female pin header, 3 pins [form="♀ (female)"]
  Part1 = SOIC18-W [part_number=DS3231 package=SOIC18-W]
  J4 = female pin header, 2 pins [form="♀ (female)"]
  C5 = Electrolytic Capacitor [capacitance=10µF package="100 mil [THT, electrolytic]"]
  J5 = female pin header, 2 pins [form="♀ (female)"]

nets:
  N1: MAX1.Data_In, J2.pin2
  N2: MAX1.Digit_0, LED115.cathode, LED125.cathode, LED136.cathode, LED148.cathode, LED154.cathode, LED161.cathode
  N3: MAX1.Digit_4, LED116.cathode, LED126.cathode, LED137.cathode, LED149.cathode, LED153.cathode, LED164.cathode
  N4: MAX1.Digit_6, LED127.cathode, LED138.cathode, LED147.cathode, LED152.cathode, LED162.cathode
  N5: MAX1.Digit_2, LED117.cathode, LED118.cathode, LED119.cathode, LED120.cathode, LED121.cathode, LED122.cathode, LED123.cathode, LED124.cathode
  N6: MAX1.Digit_3, LED128.cathode, LED129.cathode, LED130.cathode, LED131.cathode, LED132.cathode, LED133.cathode, LED134.cathode, LED135.cathode
  N7: MAX1.Digit_7, LED139.cathode, LED140.cathode, LED141.cathode, LED142.cathode, LED143.cathode, LED144.cathode, LED145.cathode, LED146.cathode
  N8: MAX1.Digit_5, LED150.cathode, LED151.cathode, LED155.cathode, LED156.cathode, LED157.cathode, LED158.cathode, LED159.cathode, LED160.cathode
  N9: MAX1.Digit_1, LED163.cathode, LED165.cathode, LED166.cathode, LED167.cathode, LED168.cathode, LED169.cathode, LED170.cathode, LED171.cathode
  N10: MAX1.Chip_Select_(CS), J2.pin1
  N11: MAX1.Cock, J2.pin3
  N12: MAX1.Segment_A, LED124.anode, LED135.anode, LED143.anode, LED158.anode, LED161.anode, LED162.anode, LED164.anode, LED168.anode
  N13: MAX1.Segment_F, LED123.anode, LED134.anode, LED141.anode, LED147.anode, LED148.anode, LED149.anode, LED155.anode, LED167.anode
  N14: MAX1.Segment_B, LED122.anode, LED133.anode, LED145.anode, LED150.anode, LED152.anode, LED153.anode, LED154.anode, LED169.anode
  N15: MAX1.Segment_G, LED121.anode, LED132.anode, LED136.anode, LED137.anode, LED138.anode, LED140.anode, LED156.anode, LED170.anode
  N16: MAX1.Iset, R1.Pin_0
  N17: MAX1.V+, R1.Pin_1, C1.0, MAX2.V+, R2.Pin_0, C3.1, C4.+, Part1.Vcc, J4.pin1, C5.+
  N18: MAX1.Segment_C, LED117.anode, LED128.anode, LED144.anode, LED160.anode, LED163.anode
  N19: MAX1.Segment_E, LED118.anode, LED129.anode, LED146.anode, LED159.anode, LED166.anode
  N20: MAX1.Segment_DP, LED115.anode, LED116.anode, LED119.anode, LED130.anode, LED139.anode, LED151.anode, LED171.anode
  N21: MAX1.Segment_D, LED120.anode, LED125.anode, LED126.anode, LED127.anode, LED131.anode, LED142.anode, LED157.anode, LED165.anode
  N22: C1.1, C3.0, C4.-, Part1.2, Part1.3, Part1.4, Part1.5, Part1.GND, Part1.14, Part1.15, Part1.16, Part1.17, J4.pin2, C5.-
  N23: MAX2.Data_In, J3.pin2
  N24: MAX2.Digit_0, LED182.cathode, LED190.cathode, LED200.cathode, LED206.cathode, LED224.cathode, LED228.cathode
  N25: MAX2.Digit_4, LED180.cathode, LED193.cathode, LED202.cathode, LED209.cathode, LED220.cathode
  N26: MAX2.Digit_6, LED172.cathode, LED173.cathode, LED174.cathode, LED175.cathode, LED176.cathode, LED177.cathode, LED178.cathode, LED179.cathode
  N27: MAX2.Digit_2, LED183.cathode, LED184.cathode, LED185.cathode, LED186.cathode, LED187.cathode, LED188.cathode, LED191.cathode, LED192.cathode
  N28: MAX2.Digit_3, LED194.cathode, LED195.cathode, LED196.cathode, LED197.cathode, LED198.cathode, LED199.cathode, LED203.cathode, LED204.cathode
  N29: MAX2.Digit_7, LED205.cathode, LED207.cathode, LED208.cathode, LED210.cathode, LED211.cathode, LED212.cathode, LED213.cathode, LED214.cathode
  N30: MAX2.Digit_5, LED216.cathode, LED218.cathode, LED219.cathode, LED221.cathode, LED222.cathode, LED223.cathode, LED225.cathode, LED226.cathode
  N31: MAX2.Digit_1, LED181.cathode, LED189.cathode, LED201.cathode, LED215.cathode, LED217.cathode, LED227.cathode
  N32: MAX2.Chip_Select_(CS), J3.pin1
  N33: MAX2.Cock, J3.pin3
  N34: MAX2.Segment_A, LED179.anode, LED184.anode, LED199.anode, LED207.anode, LED217.anode, LED220.anode, LED221.anode, LED224.anode
  N35: MAX2.Segment_F, LED178.anode, LED191.anode, LED194.anode, LED206.anode, LED209.anode, LED211.anode, LED215.anode, LED225.anode
  N36: MAX2.Segment_B, LED177.anode, LED185.anode, LED197.anode, LED200.anode, LED201.anode, LED202.anode, LED208.anode, LED218.anode
  N37: MAX2.Segment_G, LED176.anode, LED188.anode, LED189.anode, LED190.anode, LED193.anode, LED204.anode, LED210.anode, LED226.anode
  N38: MAX2.Iset, R2.Pin_1
  N39: MAX2.Segment_C, LED172.anode, LED183.anode, LED195.anode, LED213.anode, LED222.anode, LED227.anode, LED228.anode
  N40: MAX2.Segment_E, LED173.anode, LED186.anode, LED203.anode, LED214.anode, LED216.anode
  N41: MAX2.Segment_DP, LED174.anode, LED187.anode, LED198.anode, LED205.anode, LED219.anode
  N42: MAX2.Segment_D, LED175.anode, LED180.anode, LED181.anode, LED182.anode, LED192.anode, LED196.anode, LED212.anode, LED223.anode
  N43: Part1.SDA, J5.pin2
  N44: Part1.SCL, J5.pin1

notes:
  Load
  din
  clk
  sda
  scl
  vBat
  5v

custom parts:
  MAX7219: Serially Interfaced, 8-Digit, LED Display Drivers
  White 1210 smd LED: A generic white LED (~3.2V)
